# Fritzing sketch BluPill and BreadBoard 5V (saved by Fritzing 0.9.2b)
breadboards: 1

parts:
  Componente1 = BluePill
  Componente2 = Breadboard Power Supply Board SMD
  S1 = Momentary Switch [package=ksa_sealed_tac_switch]

nets:
  GND3: Componente1.GND3, Componente2.GND, S1.2
  5V: Componente1.5V, Componente2.VIN
  N1: Componente1.B5, S1.1, S1.3
